# Fritzing sketch fanta (saved by Fritzing 0.9.0b)
circuit board: 8.64534cm x 6.47979cm
circuit board: 9.03111cm x 5.09411cm
breadboards: 1

parts:
  Q1 = npn-Powertransistor [package="TO220 [THT]"]
  Q2 = npn-Powertransistor [package="TO220 [THT]"]
  Q3 = npn-Powertransistor [package="TO220 [THT]"]
  Power_plug1 = Power plug
  Power_plug3 = Power plug
  Power_plug4 = Power plug
  Power_plug2 = Power plug
  R1 = Resistor [tolerance=±5% resistance=0 package=THT]
  R2 = Resistor [tolerance=±5% resistance=0 package=THT]
  Part1 = Arduino Uno (Rev3)
  Power_plug5 = Power plug
  R3 = Resistor [tolerance=±5% resistance=10M package=THT]

nets:
  N1: Q1.collector, Power_plug2.GND
  N2: Q1.emitter, Q2.emitter, Q3.emitter, Power_plug1.GND
  N3: Q2.base, R2.Pin_1
  N4: Q2.collector, Power_plug3.GND
  N5: Q3.base, R1.Pin_1
  N6: Q3.collector, Power_plug4.GND
  VCC: Power_plug1.VCC, Power_plug3.VCC, Power_plug4.VCC, Power_plug2.VCC
  N7: Part1.A0, Power_plug5.VCC, R3.Pin_1
  GND: Part1.GND, Power_plug5.GND, R3.Pin_0
